# Fritzing sketch Messen_Spannung (saved by Fritzing 0.8.0b)

parts:
  R1 = Resistor [tolerance=±5% resistance=220 package=THT]
  LED1 = LED - 5mm [color="Red (633nm)" package="5 mm [THT]"]
  Arduino1 = Arduino Uno (Rev3)

nets:
  N1: R1.Pin_1, LED1.anode
  N2: LED1.cathode, Arduino1.GND
