# Fritzing sketch Servo (saved by Fritzing 0.8.0b)
breadboards: 2

parts:
  Pot = Rotary Potentiometer (Small) [maximum_resistance=100kΩ]
  J1 = Basic Servo
  Bauteil1 = Arduino Uno (Rev3)

nets:
  GND: Pot.leg1, J1.gnd, Bauteil1.GND
  N1: Pot.wiper, Bauteil1.A0
  VCC: Pot.leg2, J1.vcc, Bauteil1.5V
  N2: J1.pulse, Bauteil1.D9_PWM
