# Fritzing sketch Synthesizer (saved by Fritzing 0.8.0b)
breadboards: 2

parts:
  R3 = Resistor [tolerance=±5% resistance=220 package=THT]
  R2 = Rotary Potentiometer (Small)
  R1 = Rotary Potentiometer (Small)
  Arduino1 = Arduino Uno (Rev3)
  SG1 = Buzzer 12mm [package=buzzer-12mm-ns]

nets:
  N1: R3.Pin_0, SG1.1
  N2: R3.Pin_1, R2.leg1, R1.leg1, Arduino1.GND
  N3: R2.wiper, Arduino1.A0
  N4: R2.leg2, R1.leg2, Arduino1.5V
  N5: R1.wiper, Arduino1.A1
  N6: Arduino1.D8, SG1.2

custom parts:
  Buzzer 12mm: Buzzer 12mm Spark Fun Electronics SKU : Comp-Buzzer
