# Fritzing sketch Orakelwürfel_01 (saved by Fritzing 0.7.13b)
breadboards: 2

parts:
  Arduino1 = Arduino
  R1 = Resistor [tolerance=±5% resistance=100k package=THT]
  Ja_aber_mit_Stil! = LED - 5mm [color="Red (633nm)" package="5 mm [THT]"]
  R2 = Resistor [tolerance=±5% resistance=220 package=THT]
  R3 = Resistor [tolerance=±5% resistance=220 package=THT]
  R4 = Resistor [tolerance=±5% resistance=220 package=THT]
  Nein_lieber_nicht = LED - 5mm [color="Red (633nm)" package="5 mm [THT]"]
  Folge_deinem_Herzen = LED - 5mm [color="Red (633nm)" package="5 mm [THT]"]
  Warte_noch_etwas_damit = LED - 5mm [color="Red (633nm)" package="5 mm [THT]"]
  Unbedingt!_Sofort! = LED - 5mm [color="Red (633nm)" package="5 mm [THT]"]
  Tilt = Tilt Switch [package=THT]
  R5 = Resistor [tolerance=±5% resistance=220 package=THT]
  R6 = Resistor [tolerance=±5% resistance=220 package=THT]

nets:
  N1: Arduino1.GND, Ja_aber_mit_Stil!.cathode, Nein_lieber_nicht.cathode, Folge_deinem_Herzen.cathode, Warte_noch_etwas_damit.cathode, Unbedingt!_Sofort!.cathode, Tilt.Pin_1
  N2: Arduino1.D12, R2.Pin_1
  N3: Arduino1.D11, R3.Pin_1
  N4: Arduino1.D10, R4.Pin_1
  N5: Arduino1.D9, R5.Pin_1
  N6: Arduino1.D8, R6.Pin_1
  N7: Arduino1.D3, R1.Pin_0, Tilt.Pin_2
  N8: Arduino1.+5V, R1.Pin_1
  N9: Ja_aber_mit_Stil!.anode, R2.Pin_0
  N10: R3.Pin_0, Nein_lieber_nicht.anode
  N11: R4.Pin_0, Folge_deinem_Herzen.anode
  N12: Warte_noch_etwas_damit.anode, R5.Pin_0
  N13: Unbedingt!_Sofort!.anode, R6.Pin_0

notes:
  Stelle
  deine
  Frage
