# Fritzing sketch SchematicsRref (saved by Fritzing 0.8.0b)

parts:
  Arduino1 = Arduino Uno (Rev3)
  R1 = Resistor [tolerance=±5% resistance=100k package=THT]
  R5 = Rotary Potentiometer (Small)
  R6 = Photocell (LDR) [package=THT]
  Arduino2 = Arduino Uno (Rev3)

nets:
  N1: Arduino1.A0, R1.Pin_0, R6.pin_0
  N2: Arduino1.ioref, Arduino1.N/C
  N3: Arduino1.5V, R6.pin_1
  N4: Arduino1.GND, R1.Pin_1
  N5: R5.leg1, Arduino2.GND
  N6: R5.wiper, Arduino2.A0
  N7: R5.leg2, Arduino2.5V

notes:
  5V+
  GND
