# Fritzing sketch 555Keyfob (saved by Fritzing 0.8.0b)
breadboards: 2

parts:
  555 = 555 Timer [package="DIP8 [THT]"]
  Servo = Basic Servo
  C2 = Ceramic Capacitor [capacitance=22nF package="100 mil [THT, multilayer]"]
  R1 = Resistor [tolerance=±5% resistance=3.3M package=THT]
  R2 = Resistor [tolerance=±5% resistance=56k package=THT]
  Potentiometer_100k = Rotary Potentiometer (Small)
  -5V+ = Battery
  Diode = Rectifier Diode [part_number=1N4001 package="300 mil [THT]"]

nets:
  N1: 555.Ground, Servo.gnd, C2.0, -5V+.-
  N2: 555.Trigger, 555.Threshold, C2.1, R1.Pin_0, Diode.cathode
  N3: 555.Output, Servo.pulse
  N4: 555.Reset, 555.Vcc_Supply_Voltage, Servo.vcc, R2.Pin_1, -5V+.+
  N5: 555.Discharge, R1.Pin_1, Potentiometer_100k.leg1, Potentiometer_100k.wiper, Diode.anode
  N6: R2.Pin_0, Potentiometer_100k.leg2

notes:
  <GND!
