# Fritzing sketch Blink (saved by Fritzing 0.8.0b)

parts:
  LED = LED - 5mm [color="Red (633nm)" package="5 mm [THT]"]
  Arduino1 = Arduino Uno (Rev3)

nets:
  N1: LED.cathode, Arduino1.GND
  N2: LED.anode, Arduino1.D13/SCK
