# Fritzing sketch Piezo_Synth_Sch (saved by Fritzing 0.7.12b)
breadboards: 2

parts:
  Arduino1 = Arduino
  R4 = Rotary Potentiometer (Small) [maximum_resistance=100kΩ]
  R5 = Rotary Potentiometer (Small) [maximum_resistance=100kΩ]
  J1 = Piezo Speaker

nets:
  N1: Arduino1.GND, R4.leg1, R5.leg1, J1.pin2
  N2: Arduino1.D8, J1.pin1
  N3: Arduino1.+5V, R4.leg2, R5.leg2
  N4: Arduino1.A0, R4.wiper
  N5: Arduino1.A1, R5.wiper
